// Digital circuit GDC-CS-GAL.dig as structural Verilog
module GDC_CS_GAL (
  input  nCSxBRD,
  input  bA2,
  input  bA3,
  input  nbWR,
  input  nbRD,
  input  nDBINxGDC,
  input  nALE2,
  input  _2xWCLK,
  input  HSYNC,
  input  VSYNC,
  output nCSxGDCxRD,
  output nCSxGDCxWR,
  output nCSxLATCH,
  output nCSxRAMDACxWR,
  output nCSxRAMDACxRD,
  output nCSxRAMDAC,
  output nCSxGDC,
  output nREADxVRAM,
  output nDBIN,
  output H_plus_VSYNC
);

  wire _74139_1_p11, _74139_1_p12, or_2_out;

  // _74139 _74139_1: pin names not known; wires that end beside it: nCSxBRD, bA2, bA3, 1'b1, 1'b1, 1'b1, 1'b1, 1'b0, nCSxGDC, nCSxLATCH, _74139_1_p11, _74139_1_p12
  or or_1 (nDBIN, nDBINxGDC, nDBINxGDC);
  or or_2 (or_2_out, nALE2, _2xWCLK);
  and and_1 (H_plus_VSYNC, HSYNC, VSYNC);
  and and_2 (nREADxVRAM, nDBIN, or_2_out);
  or or_3 (nCSxGDCxRD, nbRD, nCSxGDC);
  or or_4 (nCSxGDCxWR, nCSxGDC, nbWR);
  and and_3 (nCSxRAMDAC, _74139_1_p11, _74139_1_p12);
  or or_5 (nCSxRAMDACxWR, nbWR, nCSxRAMDAC);
  or or_6 (nCSxRAMDACxRD, nCSxRAMDAC, nbRD);

  // Notes on the sheet:
  //   nCSxBRD: pin 4
  //   bA2: pin 5
  //   bA3: pin 6
  //   nbWR: pin 3
  //   nbRD: pin 2
  //   nCSxGDCxRD: pin 23
  //   nCSxGDCxWR: pin 22
  //   nCSxLATCH: pin 21
  //   nCSxRAMDACxWR: pin 20
  //   nCSxRAMDACxRD: pin 19
  //   nCSxRAMDAC: pin 18
  //   nCSxGDC: pin 17
  //   nDBINxGDC: pin 7
  //   nALE2: pin 8
  //   _2xWCLK: pin 9
  //   nREADxVRAM: pin 15
  //   nDBIN: pin 16
  //   HSYNC: pin 10
  //   VSYNC: pin 11
  //   H_plus_VSYNC: pin 14
  //   GDC CS GAL22V10
endmodule
