// Digital circuit VDCENET-CS-GAL.dig as structural Verilog
module VDCENET_CS_GAL (
  input  nbWR,
  input  nbRD,
  input  nCSxVDC,
  input  nCSxENET,
  input  ENETxINT0,
  input  nbRESET,
  input  HSYNOUT,
  input  VSYNOUT,
  input  CSYNOUT,
  output CSxVDC,
  output nBUSxEN,
  output nENETxINT0,
  output RD,
  output bRESET,
  output nHSYNOUT,
  output nVSYNOUT,
  output nCSYNOUT,
  output nVDCxLED,
  output nENETxLED
);

  wire not_1_out;

  not not_1 (not_1_out, nbWR);
  not not_2 (RD, nbRD);
  not not_3 (nENETxINT0, ENETxINT0);
  not not_4 (bRESET, nbRESET);
  not not_5 (nHSYNOUT, HSYNOUT);
  not not_6 (nVSYNOUT, VSYNOUT);
  not not_7 (nCSYNOUT, CSYNOUT);
  or or_1 (CSxVDC, not_1_out, RD);
  and and_1 (nBUSxEN, nCSxVDC, nCSxENET);

  assign nENETxLED = nCSxVDC;
  assign nVDCxLED = nCSxENET;

  // Notes on the sheet:
  //   nbWR: pin 2
  //   nbRD: pin 3
  //   CSxVDC: pin 23
  //   nCSxVDC: pin 4
  //   nCSxENET: pin 5
  //   nBUSxEN: pin 21
  //   ENETxINT0: pin 6
  //   nENETxINT0: pin 20
  //   RD: pin 22
  //   nbRESET: pin 7
  //   bRESET: pin 19
  //   HSYNOUT: pin 8
  //   VSYNOUT: pin 9
  //   CSYNOUT: pin 10
  //   nHSYNOUT: pin 18
  //   nVSYNOUT: pin 17
  //   nCSYNOUT: pin 16
  //   nVDCxLED: pin 15
  //   nENETxLED: pin 14
  //   VDCENET CS GAL22V10
endmodule
