// Digital circuit SAB80535-CS-2.dig as structural Verilog
module SAB80535_CS_2 (
  input  A2,
  input  A3,
  input  A4,
  input  nY0,
  input  nWR,
  input  A1,
  input  nOE,
  output nCSxUSBxSD,
  output nCSxI2C,
  output nCSxFFxWR,
  output nCSxLATCHxOE,
  output A,
  output CSxLATCHxWR
);

  wire _74138_1_p11, _74138_1_p12;

  // _74138 _74138_1: pin names not known; wires that end beside it: A1, A2, A3, A4, 1'b0, nY0, 1'b1, 1'b0, nCSxUSBxSD, nCSxI2C, _74138_1_p11, _74138_1_p12
  or or_1 (A, nCSxI2C, nWR);
  or or_2 (nCSxFFxWR, _74138_1_p11, nWR);
  nor nor_1 (CSxLATCHxWR, _74138_1_p12, nWR);
  or or_3 (nCSxLATCHxOE, _74138_1_p12, nOE);

  // Notes on the sheet:
  //   A2: pin 5
  //   A3: pin 4
  //   A4: pin 3
  //   nCSxUSBxSD: pin 19
  //   nCSxI2C: pin 18
  //   nCSxFFxWR: pin 17
  //   nCSxLATCHxOE: pin 14
  //   nY0: pin 2
  //   nWR: pin 7
  //   A: pin 15
  //   A1: pin 6
  //   nOE: pin 8
  //   CSxLATCHxWR: pin 16
  //   SAB80535 CS 2 GAL16V8
endmodule
