// Digital circuit SAB80535-IO-SELECT.dig as structural Verilog
module SAB80535_IO_SELECT (
  input  A5,
  input  A6,
  input  A7,
  input  A15,
  input  A14,
  input  A13,
  input  A12,
  input  A11,
  input  A10,
  input  A9,
  input  A8,
  output nIOxSEL,
  output nY0,
  output nY1,
  output nY3,
  output nY4,
  output nY5,
  output nY6,
  output nY2,
  output nY7
);

  nand nand_1 (nIOxSEL, A15, A14, A13, A12, A11, A10, A9, A8);
  // _74138 _74138_1: pin names not known; wires that end beside it: A5, A6, A7, 1'b1, 1'b0, nIOxSEL, 1'b1, 1'b0, nY0, nY1, nY2, nY3, nY4, nY5, nY6, nY7

  // Notes on the sheet:
  //   nIOxSEL: pin 15
  //   A5: pin 13
  //   A6: pin 11
  //   A7: pin 10
  //   nY0: pin 23
  //   nY1: pin 22
  //   nY3: pin 20
  //   nY4: pin 19
  //   nY5: pin 18
  //   nY6: pin 17
  //   nY2: pin 21
  //   nY7: pin 16
  //   A15: pin 2
  //   A14: pin 3
  //   A13: pin 4
  //   A12: pin 5
  //   A11: pin 6
  //   A10: pin 7
  //   A9: pin 8
  //   A8: pin 9
  //   SAB80535 IO SELECT GAL22V10
endmodule
