// Digital circuit SAB80535-RX-TX.dig as structural Verilog
module SAB80535_RX_TX (
  input  nRD,
  input  nPSEN,
  input  nWR,
  input  TxD,
  input  TO,
  input  RxDx1,
  input  RxDx0,
  input  nCSxLCD,
  input  CSxLCDxWRxPRIME,
  input  RESET,
  input  A,
  output nOE,
  output CSxLCDxWR,
  output TXxLED,
  output RXxLED,
  output TxDx0,
  output TxDx1,
  output RxD,
  output E,
  output nRESET,
  output nCSxI2CxWR
);

  wire and_2_out, nor_1_out, nor_2_out, not_1_out, not_2_out, not_3_out, not_5_out, not_9_out;

  not not_1 (not_1_out, TxD);
  not not_2 (not_2_out, TO);
  not not_3 (not_3_out, CSxLCDxWRxPRIME);
  not not_4 (nRESET, RESET);
  not not_5 (not_5_out, A);
  and and_1 (nOE, nRD, nPSEN);
  and and_2 (and_2_out, nOE, nWR);
  nor nor_1 (nor_1_out, TO, RxDx1);
  nor nor_2 (nor_2_out, not_2_out, RxDx0);
  nor nor_3 (CSxLCDxWR, and_2_out, nCSxLCD);
  not not_6 (TXxLED, not_1_out);
  nand nand_1 (TxDx1, not_1_out, not_2_out);
  nand nand_2 (TxDx0, not_1_out, TO);
  nor nor_4 (RxD, nor_1_out, nor_2_out);
  not not_7 (E, not_3_out);
  not not_8 (nCSxI2CxWR, not_5_out);
  not not_9 (not_9_out, RxD);
  not not_10 (RXxLED, not_9_out);

  // Notes on the sheet:
  //   nRD: pin 2
  //   nPSEN: pin 3
  //   nOE: pin 23
  //   nWR: pin 4
  //   CSxLCDxWR: pin 22
  //   TxD: pin 6
  //   TXxLED: pin 21
  //   RXxLED: pin 17
  //   TO: pin 7
  //   TxDx0: pin 19
  //   TxDx1: pin 20
  //   RxDx1: pin 8
  //   RxDx0: pin 9
  //   RxD: pin 18
  //   nCSxLCD: pin 5
  //   CSxLCDxWRxPRIME: pin 10
  //   E: pin 16
  //   RESET: pin 11
  //   nRESET: pin 15
  //   A: pin 13
  //   nCSxI2CxWR: pin 14
  //   ~TO
  //   ~TxD
  //   SAB80535 RX TX V2 GAL22V10
  //   ~OExWR
  //   ~Rx1
  //   ~Rx0
endmodule
