// Digital circuit CPU-DATA-DIR-GAL-V3.dig as structural Verilog
module CPU_DATA_DIR_GAL_V3 (
  input  IOxSEL,
  input  nCPUxRD,
  input  nDMAxIEI1,
  input  nCPUxM1,
  input  nCPUxIORQ,
  input  nIM2xINT,
  input  nDMAxIEO2,
  input  nFPxLATCH,
  input  nCPUxWR,
  output DATAxDIR,
  output nIM2xEN,
  output nFPxLATCHxRD,
  output FPxLATCHxWR,
  output nIM2xIEO
);

  wire not_1_out, not_2_out, or_1_out, or_4_out, or_5_out, or_6_out;

  not not_1 (not_1_out, nDMAxIEO2);
  not not_2 (not_2_out, nDMAxIEO2);
  or or_1 (or_1_out, nCPUxM1, nCPUxIORQ);
  or or_2 (nIM2xIEO, nIM2xINT, not_2_out);
  or or_3 (nFPxLATCHxRD, nCPUxRD, nFPxLATCH);
  or or_4 (or_4_out, nFPxLATCH, nCPUxWR);
  or or_5 (or_5_out, nCPUxRD, IOxSEL);
  or or_6 (or_6_out, or_1_out, not_1_out);
  or or_7 (nIM2xEN, or_1_out, nIM2xIEO);
  not not_3 (FPxLATCHxWR, or_4_out);
  and and_1 (DATAxDIR, or_5_out, or_6_out);

  // Notes on the sheet:
  //   DATAxDIR: pin 23
  //   IOxSEL: pin 3
  //   nCPUxRD: pin 2
  //   nDMAxIEI1: pin 6
  //   nCPUxM1: pin 4
  //   nCPUxIORQ: pin 5
  //   nIM2xINT: pin 7
  //   nDMAxIEO2: pin 8
  //   nIM2xEN: pin 22
  //   nFPxLATCH: pin 9
  //   nFPxLATCHxRD: pin 21
  //   nCPUxWR: pin 10
  //   FPxLATCHxWR: pin 20
  //   nIM2xIEO: pin 19
  //   CPU DATA DIR V3 GAL22V10
  //   ~INTA
  //   HIGH A->B
  //   LOW B->A
endmodule
