// Digital circuit CPU-DATA-DIR-GAL-V2.dig as structural Verilog
module CPU_DATA_DIR_GAL_V2 (
  input  nDMAxIEI1,
  input  nCPUxM1,
  input  nCPUxIORQ,
  input  nIM2xINT,
  input  nDMAxIEO2,
  input  nFPxLATCH,
  input  nCPUxWR,
  input  nCPUxRD,
  input  IO_SEL,
  output DATAxDIR,
  output nIM2xEN,
  output nFPxLATCHxRD,
  output FPxLATCHxWR,
  output nIM2xIEO,
  output DMAxIEI1
);

  wire and_1_out, and_2_out, and_3_out, not_1_out, not_2_out, not_4_out, or_1_out, or_4_out;

  not not_1 (not_1_out, nDMAxIEO2);
  not not_2 (not_2_out, or_1_out);
  or or_1 (or_1_out, nCPUxM1, nCPUxIORQ);
  not not_3 (DMAxIEI1, nDMAxIEI1);
  not not_4 (not_4_out, nDMAxIEO2);
  and and_1 (and_1_out, IO_SEL, or_1_out);
  and and_2 (and_2_out, not_1_out, not_2_out);
  and and_3 (and_3_out, or_1_out, nCPUxRD);
  or or_2 (nIM2xIEO, nIM2xINT, not_4_out);
  or or_3 (nFPxLATCHxRD, nCPUxRD, nFPxLATCH);
  or or_4 (or_4_out, nFPxLATCH, nCPUxWR);
  or or_5 (DATAxDIR, and_1_out, and_2_out, and_3_out);
  or or_6 (nIM2xEN, or_1_out, nIM2xIEO);
  not not_5 (FPxLATCHxWR, or_4_out);

  // Notes on the sheet:
  //   DATAxDIR: pin 23
  //   nDMAxIEI1: pin 6
  //   nCPUxM1: pin 4
  //   nCPUxIORQ: pin 5
  //   nIM2xINT: pin 7
  //   nDMAxIEO2: pin 8
  //   nIM2xEN: pin 22
  //   nFPxLATCH: pin 9
  //   nFPxLATCHxRD: pin 21
  //   nCPUxWR: pin 10
  //   FPxLATCHxWR: pin 20
  //   nIM2xIEO: pin 19
  //   nCPUxRD: pin 2
  //   IO_SEL: pin 3
  //   DMAxIEI1: pin 18
  //   CPU DATA DIR V2 GAL22V10
  //   ~INTA
  //   HIGH A->B
  //   LOW B->A
endmodule
