// Digital circuit DMA-CS-GAL-V3.dig as structural Verilog
module DMA_CS_GAL_V3 (
  input  nDMAxADDR,
  input  CPUxA0,
  input  CPUxA1,
  input  nCPUxWAIT,
  input  nBUSRQ,
  input  nCPUxBUSACK,
  input  nDMAxINTxPULSE1,
  input  nDMAxINTxPULSE2,
  input  nCSxIO,
  input  CPUxA3,
  input  nDMAxBAO2,
  output nFPxLATCH,
  output nCExDMAxRDY,
  output nDMAxCS1,
  output nDMAxCS2,
  output nBUSxEN,
  output DATAxXFER,
  output IOxSEL,
  output nCSxMAP,
  output nCSxUART
);

  wire _74139_1_p9, _74139_1_p10, _74157_1_p13, _74157_1_p14, and_1_out, not_1_out, not_2_out, not_3_out,
       or_1_out;

  not not_1 (not_1_out, CPUxA3);
  // _74139 _74139_1: pin names not known; wires that end beside it: 1'b1, 1'b1, 1'b1, nDMAxADDR, CPUxA0, CPUxA1, 1'b1, 1'b0, _74139_1_p9, _74139_1_p10, nFPxLATCH, nCExDMAxRDY
  // _74157 _74157_1: pin names not known; wires that end beside it: nCPUxWAIT, nCPUxWAIT, 1'b0, 1'b0, _74139_1_p9, _74139_1_p10, 1'b0, 1'b0, nBUSRQ, 1'b0, 1'b1, 1'b0, _74157_1_p13, _74157_1_p14
  not not_2 (not_2_out, nDMAxBAO2);
  not not_3 (not_3_out, nCPUxBUSACK);
  or or_1 (or_1_out, nCPUxBUSACK, nBUSRQ);
  and and_1 (and_1_out, nDMAxINTxPULSE1, nDMAxINTxPULSE2);
  nand nand_1 (IOxSEL, nDMAxADDR, nCSxIO);
  or or_2 (nCSxMAP, nCSxIO, CPUxA3);
  or or_3 (nCSxUART, nCSxIO, not_1_out);
  or or_4 (nDMAxCS1, not_3_out, _74157_1_p13);
  or or_5 (nDMAxCS2, not_3_out, _74157_1_p14);
  or or_6 (nBUSxEN, nCPUxBUSACK, not_2_out);
  or or_7 (DATAxXFER, or_1_out, and_1_out);

  // Notes on the sheet:
  //   nDMAxADDR: pin 2
  //   CPUxA0: pin 3
  //   CPUxA1: pin 4
  //   nFPxLATCH: pin 23
  //   nCExDMAxRDY: pin 22
  //   nCPUxWAIT: pin 6
  //   nBUSRQ: pin 7
  //   nCPUxBUSACK: pin 5
  //   nDMAxCS1: pin 21
  //   nDMAxCS2: pin 20
  //   nBUSxEN: pin 19
  //   nDMAxINTxPULSE1: pin 8
  //   nDMAxINTxPULSE2: pin 9
  //   DATAxXFER: pin 18
  //   nCSxIO: pin 10
  //   IOxSEL: pin 17
  //   CPUxA3: pin 11
  //   nCSxMAP: pin 16
  //   nCSxUART: pin 15
  //   nDMAxBAO2: pin 13
  //   DMA CS V3 GAL22V10
  //   HACK!!!  ~BUS-EN should be asserted (low)
  //   except when ~BUS-ACK is asserted (low)
  //   and ~BAO is not asserted (high).  We don't
  //   have ~BAO, so force ~BUS-EN asserted (low)
  //   all the time.
endmodule
