// Digital circuit ZP-DATA-DIR-GAL-V2.dig as structural Verilog
module ZP_DATA_DIR_GAL_V2 (
  input  nCS1,
  input  nbIEI,
  input  bA2,
  input  bA3,
  input  nbRD,
  input  nbM1,
  input  nbIORQ,
  input  nbRESET,
  input  nIEO,
  input  BASE_CLK,
  input  nCS2,
  output DATA_DIR,
  output nCSxCTC1,
  output nCSxSIO1,
  output nCSxPIO1,
  output nCSxPIO2,
  output nPM1,
  output CLKxZILOG
);

  wire nand_1_out, nand_2_out, not_1_out, not_2_out, not_3_out, not_4_out, not_5_out, not_6_out, or_1_out;

  not not_1 (not_1_out, nCS2);
  not not_2 (not_2_out, nbRD);
  not not_3 (not_3_out, nCS1);
  not not_4 (not_4_out, nIEO);
  not not_5 (not_5_out, nbM1);
  not not_6 (not_6_out, nbIORQ);
  or or_1 (or_1_out, not_1_out, not_3_out);
  and and_1 (nPM1, nbRESET, nbM1);
  nand nand_1 (nand_1_out, not_2_out, or_1_out, not_6_out);
  nand nand_2 (nand_2_out, not_4_out, not_5_out, nbIEI, not_6_out);
  // _74138 _74138_1: pin names not known; wires that end beside it: 1'b1, 1'b0, not_3_out, nbIORQ, nbIORQ, bA2, bA3, 1'b0, nCSxCTC1, nCSxSIO1, nCSxPIO1, nCSxPIO2
  and and_2 (CLKxZILOG, BASE_CLK, BASE_CLK);
  and and_3 (DATA_DIR, nand_1_out, nand_2_out);

  // Notes on the sheet:
  //   nCS1: pin 4
  //   nbIEI: pin 7
  //   DATA_DIR: pin 22
  //   bA2: pin 9
  //   bA3: pin 10
  //   nbRD: pin 3
  //   nbM1: pin 6
  //   nbIORQ: pin 8
  //   nCSxCTC1: pin 21
  //   nCSxSIO1: pin 20
  //   nCSxPIO1: pin 19
  //   nCSxPIO2: pin 18
  //   nbRESET: pin 2
  //   nPM1: pin 23
  //   nIEO: pin 5
  //   BASE_CLK: pin 11
  //   CLKxZILOG: pin 17
  //   nCS2: pin 13
  //   ZILOG DATA DIR V2 GAL22V10
  //   IA
endmodule
