// Digital circuit CPU-MAPPER-V3.dig as structural Verilog
module CPU_MAPPER_V3 (
  input  nCPUxWR,
  input  CPU_A2,
  input  nCSxMAP,
  input  CPU_A14,
  input  mA14,
  input  CPU_A15,
  input  mA15,
  input  nCPUxIORQ,
  input  CPU_A1,
  input  nINTxI2C,
  input  nA,
  output nPAGExWR,
  output nPGENxWR,
  output SEL_A14,
  output SEL_A15,
  output nCSxI2C,
  output INT_I2C,
  output nCSxI2CxWR,
  output nA_2
);

  wire _74139_1_p10, _74139_1_p11, not_1_out;

  not not_1 (not_1_out, CPU_A1);
  not not_2 (INT_I2C, nINTxI2C);
  // _74139 _74139_1: pin names not known; wires that end beside it: nCPUxWR, CPU_A2, nCSxMAP, 1'b0, CPU_A2, nCSxMAP, 1'b1, 1'b0, nPAGExWR, _74139_1_p10, _74139_1_p11
  // _74157 _74157_1: pin names not known; wires that end beside it: CPU_A14, CPU_A15, 1'b1, 1'b1, mA14, mA15, 1'b1, 1'b1, nCPUxIORQ, 1'b0, 1'b1, 1'b0, SEL_A14, SEL_A15
  or or_1 (nPGENxWR, _74139_1_p10, CPU_A1);
  or or_2 (nCSxI2C, _74139_1_p11, not_1_out);
  or or_3 (nA_2, nCSxI2C, nCPUxWR);

  assign nCSxI2CxWR = nA;

  // Notes on the sheet:
  //   nCPUxWR: pin 2
  //   CPU_A2: pin 3
  //   nCSxMAP: pin 4
  //   nPAGExWR: pin 23
  //   nPGENxWR: pin 20
  //   CPU_A14: pin 5
  //   mA14: pin 7
  //   CPU_A15: pin 6
  //   mA15: pin 8
  //   nCPUxIORQ: pin 9
  //   SEL_A14: pin 22
  //   SEL_A15: pin 21
  //   nCSxI2C: pin 19
  //   CPU_A1: pin 10
  //   nINTxI2C: pin 11
  //   INT_I2C: pin 18
  //   nCSxI2CxWR: pin 17
  //   nA: pin 13
  //   nA_2: pin 14
  //   CPU MAPPER V3 GAL22V10
endmodule
