// Digital circuit CPU-MAPPER.dig as structural Verilog
module CPU_MAPPER (
  input  nCPUxWR,
  input  CPU_A2,
  input  nCSxMAP,
  input  CPU_A14,
  input  mA14,
  input  CPU_A15,
  input  mA15,
  input  nCPUxIORQ,
  output nPAGExWR,
  output nPGENxWR,
  output SEL_A14,
  output SEL_A15
);

  // _74139 _74139_1: pin names not known; wires that end beside it: nCPUxWR, CPU_A2, nCSxMAP, 1'b1, 1'b1, 1'b1, 1'b1, 1'b0, nPAGExWR, nPGENxWR
  // _74157 _74157_1: pin names not known; wires that end beside it: CPU_A14, CPU_A15, 1'b1, 1'b1, mA14, mA15, 1'b1, 1'b1, nCPUxIORQ, 1'b0, 1'b1, 1'b0, SEL_A14, SEL_A15

  // Notes on the sheet:
  //   nCPUxWR: pin 2
  //   CPU_A2: pin 3
  //   nCSxMAP: pin 4
  //   nPAGExWR: pin 19
  //   nPGENxWR: pin 18
  //   CPU_A14: pin 5
  //   mA14: pin 7
  //   CPU_A15: pin 6
  //   mA15: pin 8
  //   nCPUxIORQ: pin 9
  //   SEL_A14: pin 17
  //   SEL_A15: pin 16
  //   CPU MAPPER GAL16V8
endmodule
