// Digital circuit ROMRAM-GAL2.dig as structural Verilog
module ROMRAM_GAL2 (
  input  nMEMxEN,
  input  nBOOT,
  input  nCSxRTC,
  input  nbMREQ,
  input  nbM1,
  input  nbIORQ,
  input  nbRD,
  input  nbWR,
  output nBUSxEN,
  output nIOxEN,
  output nCSxMEM,
  output nRTCxRD,
  output nRTCxWR
);

  wire and_1_out, and_2_out, and_3_out, and_4_out, not_1_out, not_2_out, not_3_out, not_4_out, not_5_out,
       xor_1_out;

  not not_1 (not_1_out, nbM1);
  not not_2 (not_2_out, nMEMxEN);
  not not_3 (not_3_out, nBOOT);
  not not_4 (not_4_out, nCSxRTC);
  not not_5 (not_5_out, nbMREQ);
  and and_1 (and_1_out, nBOOT, not_2_out, not_5_out);
  and and_2 (and_2_out, not_3_out, nMEMxEN, not_5_out);
  and and_3 (and_3_out, not_4_out, not_5_out);
  and and_4 (and_4_out, nCSxRTC, nbMREQ);
  or or_1 (nIOxEN, not_1_out, nbIORQ);
  xor xor_1 (xor_1_out, nBOOT, nMEMxEN);
  or or_2 (nRTCxRD, nbRD, nCSxRTC);
  or or_3 (nRTCxWR, nCSxRTC, nbWR);
  or or_4 (nBUSxEN, and_1_out, and_2_out, and_3_out, and_4_out);
  or or_5 (nCSxMEM, xor_1_out, nbMREQ);

  // Notes on the sheet:
  //   nBUSxEN: pin 23
  //   nMEMxEN: pin 5
  //   nBOOT: pin 4
  //   nCSxRTC: pin 3
  //   nbMREQ: pin 2
  //   nbM1: pin 6
  //   nbIORQ: pin 7
  //   nIOxEN: pin 22
  //   nCSxMEM: pin 21
  //   nbRD: pin 8
  //   nbWR: pin 9
  //   nRTCxRD: pin 20
  //   nRTCxWR: pin 19
  //   ROM & RAM GAL22V10
endmodule
