// Digital circuit ZP-IA-DELAY-GAL.dig as structural Verilog
module ZP_IA_DELAY_GAL (
  input  nbIORQxRAW,
  input  nbM1,
  input  DELxCNT,
  input  bCLK,
  output nbIORQ,
  output nbWAIT,
  output bM1,
  output nbCLK
);

  wire not_1_out, not_4_out, not_5_out, or_1_out;

  not not_1 (not_1_out, nbIORQxRAW);
  not not_2 (bM1, nbM1);
  not not_3 (nbCLK, bCLK);
  not not_4 (not_4_out, not_1_out);
  or or_1 (or_1_out, DELxCNT, nbM1);
  not not_5 (not_5_out, or_1_out);
  or or_2 (nbIORQ, not_4_out, not_5_out);
  or or_3 (nbWAIT, not_4_out, or_1_out);

  // Notes on the sheet:
  //   nbIORQxRAW: pin 2
  //   nbM1: pin 4
  //   DELxCNT: pin 3
  //   bCLK: pin 5
  //   nbIORQ: pin 19
  //   nbWAIT: pin 18
  //   bM1: pin 17
  //   nbCLK: pin 16
  //   ZILOG INTERRUPT ACKNOWLEDGE DELAY GAL16V8
endmodule
