// Digital circuit multi-GAL1.dig as structural Verilog
module multi_GAL1 (
  input  nCSxPAR,
  input  bA0,
  input  bA1,
  input  bA2,
  input  nbRD,
  input  nbWR,
  input  PARINT,
  input  ACK,
  input  nCSxDUART,
  input  P24_OB,
  input  P25_BF,
  output nPARIN0,
  output nPARIN1,
  output nPARIN2,
  output nPAROUT0,
  output nPAROUT2,
  output nCSxKM,
  output nCSxUS,
  output INTxPAR,
  output nBUSxEN,
  output INTxKM
);

  wire _74138_1_p9, _74138_1_p10, _74138_1_p11, _74138_1_p12, _74138_1_p13, _74138_1_p14, _74138_1_p15,
       not_1_out, not_2_out;

  not not_1 (not_1_out, ACK);
  and and_1 (INTxPAR, PARINT, not_1_out);
  or or_1 (INTxKM, P24_OB, P25_BF);
  not not_2 (not_2_out, nCSxPAR);
  // _74138 _74138_1: pin names not known; wires that end beside it: bA0, bA1, bA2, not_2_out, nCSxPAR, nCSxPAR, 1'b1, 1'b0, _74138_1_p9, _74138_1_p10, _74138_1_p11, _74138_1_p12, _74138_1_p13, _74138_1_p14, _74138_1_p15
  or or_2 (nPARIN0, nbRD, _74138_1_p9);
  or or_3 (nPARIN1, nbRD, _74138_1_p10);
  or or_4 (nPARIN2, nbRD, _74138_1_p11);
  or or_5 (nPAROUT0, nbWR, _74138_1_p9);
  or or_6 (nPAROUT2, nbWR, _74138_1_p11);
  and and_2 (nCSxKM, _74138_1_p12, _74138_1_p13);
  and and_3 (nCSxUS, _74138_1_p14, _74138_1_p15);
  and and_4 (nBUSxEN, nCSxPAR, nCSxDUART);

  // Notes on the sheet:
  //   nCSxPAR: pin 7
  //   bA0: pin 4
  //   bA1: pin 5
  //   bA2: pin 6
  //   nbRD: pin 2
  //   nbWR: pin 3
  //   nPARIN0: pin 23
  //   nPARIN1: pin 22
  //   nPARIN2: pin 21
  //   nPAROUT0: pin 20
  //   nPAROUT2: pin 19
  //   nCSxKM: pin 18
  //   nCSxUS: pin 17
  //   PARINT: pin 9
  //   ACK: pin 10
  //   INTxPAR: pin 15
  //   nBUSxEN: pin 16
  //   nCSxDUART: pin 8
  //   P24_OB: pin 11
  //   P25_BF: pin 13
  //   INTxKM: pin 14
  //   MULTI IO GAL22V10
endmodule
