// Digital circuit DISK-CS-GAL.dig as structural Verilog
module DISK_CS_GAL (
  input  nCSxDISK,
  input  bA3,
  input  bA2,
  input  nbRD,
  input  nbWR,
  input  nCSxENET,
  output nCSxFDC,
  output nCSxPPIDE,
  output nSPIxRD,
  output nSPIxWR,
  output nCSxSPIxLED,
  output nCSxPPIDExLED,
  output nBUSxEN
);

  wire not_1_out, not_2_out, or_2_out, or_6_out;

  not not_1 (not_1_out, bA3);
  or or_1 (nCSxFDC, nCSxDISK, bA3);
  or or_2 (or_2_out, nCSxDISK, not_1_out);
  or or_3 (nSPIxRD, nbRD, or_6_out);
  or or_4 (nSPIxWR, or_6_out, nbWR);
  not not_2 (not_2_out, bA2);
  or or_5 (nCSxPPIDE, or_2_out, bA2);
  or or_6 (or_6_out, or_2_out, not_2_out);
  or or_7 (nCSxSPIxLED, or_6_out, or_6_out);
  or or_8 (nCSxPPIDExLED, nCSxPPIDE, nCSxPPIDE);
  and and_1 (nBUSxEN, nCSxDISK, nCSxENET);

  // Notes on the sheet:
  //   nCSxDISK: pin 2
  //   bA3: pin 3
  //   nCSxFDC: pin 19
  //   nCSxPPIDE: pin 18
  //   bA2: pin 4
  //   nbRD: pin 5
  //   nbWR: pin 6
  //   nSPIxRD: pin 17
  //   nSPIxWR: pin 16
  //   nCSxSPIxLED: pin 15
  //   nCSxPPIDExLED: pin 14
  //   nCSxENET: pin 7
  //   nBUSxEN: pin 13
  //   DISK CS GAL16V8
  //   ~CSxSPI
endmodule
