// Digital circuit FDC-DMA-GAL.dig as structural Verilog
module FDC_DMA_GAL (
  input  nbRESET,
  input  nCSxFDC,
  input  bA0,
  input  bA1,
  input  bA2,
  input  nPULSE,
  input  nbWR,
  input  nbRD,
  output FDCxRESET,
  output FDCxTC,
  output nMSRxDATA,
  output nLDCR,
  output nLDOR,
  output nFDCxDACK,
  output nCSxFDCxLED,
  output nCSxTTS
);

  wire _74138_1_p9, _74138_1_p10, _74138_1_p11, _74138_1_p12, _74138_1_p15, _74138_1_p16, or_1_out, or_2_out;

  or or_1 (or_1_out, nPULSE, nPULSE);
  nand nand_1 (FDCxRESET, nbRESET, nbRESET, _74138_1_p12);
  nand nand_2 (FDCxTC, or_1_out, _74138_1_p16, _74138_1_p11);
  // _74138 _74138_1: pin names not known; wires that end beside it: 1'b1, 1'b0, 1'b1, nCSxFDC, nCSxFDC, bA0, bA1, bA2, _74138_1_p9, _74138_1_p10, _74138_1_p11, _74138_1_p12, nCSxTTS, nLDCR, _74138_1_p15, _74138_1_p16
  or or_2 (or_2_out, nbRD, _74138_1_p15);
  or or_3 (nLDOR, _74138_1_p15, nbWR);
  and and_1 (nMSRxDATA, _74138_1_p9, _74138_1_p10);
  and and_2 (nFDCxDACK, _74138_1_p16, or_2_out);
  and and_3 (nCSxFDCxLED, nCSxFDC, nCSxFDC);

  // Notes on the sheet:
  //   nbRESET: pin 2
  //   nCSxFDC: pin 4
  //   bA0: pin 5
  //   bA1: pin 6
  //   bA2: pin 7
  //   FDCxRESET: pin 19
  //   FDCxTC: pin 18
  //   nMSRxDATA: pin 17
  //   nLDCR: pin 15
  //   nPULSE: pin 3
  //   nbWR: pin 9
  //   nbRD: pin 8
  //   nLDOR: pin 13
  //   nFDCxDACK: pin 14
  //   nCSxFDCxLED: pin 12
  //   nCSxTTS: pin 16
  //   ~TEND
  //   FDC DMA GAL16V8
  //   ~DACKxANDxTC
  //   ~USERxRESET
  //   ~TC
  //   ~DACK
endmodule
