// Digital circuit flip-flop-as-inverter.dig as structural Verilog
module flip_flop_as_inverter (
  input  nPRE,
  output Q,
  output nQ
);

  _7474 _7474_1 (
    .pin1(1'b0), .pin2(1'b0), .pin3(1'b0), .pin4(nPRE), .pin5(Q), .pin6(nQ), .pin7(1'b0), .pin10(1'b1),
    .pin11(1'b1), .pin12(1'b1), .pin13(1'b1), .pin14(1'b1));  // open: pin8, pin9
endmodule
