// Digital circuit VOICE-CS-GAL-V3.dig as structural Verilog
module VOICE_CS_GAL_V3 (
  input  nBRDxSEL,
  input  bA0,
  input  bA1,
  input  bA2,
  input  A15xTTS,
  input  nbWR,
  output nCSxDACxWR,
  output nCSxADC,
  output nCSxTTS,
  output nCSxSN1,
  output nCSxSN2,
  output CSxTTS,
  output nA15,
  output nCSxADCxWR
);

  wire _74138_1_p9, _74138_1_p11, _74138_1_p12, _74138_1_p13;

  // _74138 _74138_1: pin names not known; wires that end beside it: 1'b1, 1'b0, 1'b1, nBRDxSEL, nBRDxSEL, bA0, bA1, bA2, _74138_1_p9, nCSxADC, _74138_1_p11, _74138_1_p12, _74138_1_p13
  or or_1 (nCSxDACxWR, _74138_1_p11, nbWR);
  or or_2 (nCSxSN1, _74138_1_p12, nbWR);
  or or_3 (nCSxSN2, _74138_1_p13, nbWR);
  or or_4 (CSxTTS, _74138_1_p9, nbWR);
  or or_5 (nCSxADCxWR, nbWR, nCSxADC);
  not not_1 (nA15, A15xTTS);

  assign nCSxTTS = CSxTTS;

  // Notes on the sheet:
  //   nCSxDACxWR: pin 17
  //   nCSxADC: pin 18
  //   nCSxTTS: pin 19
  //   nCSxSN1: pin 16
  //   nCSxSN2: pin 15
  //   nBRDxSEL: pin 2
  //   bA0: pin 4
  //   bA1: pin 3
  //   bA2: pin 5
  //   CSxTTS: pin 14
  //   A15xTTS: pin 7
  //   nA15: pin 12
  //   nbWR: pin 6
  //   nCSxADCxWR: pin 13
  //   VOICE CS V3 GAL16V8
endmodule
