// Digital circuit MEDIA-CS-V2-GAL.dig as structural Verilog
module MEDIA_CS_V2_GAL (
  input  nCSxMEDIA,
  input  bA2,
  input  bA1,
  input  nbWR,
  input  bA0,
  input  nbRD,
  input  nIDELAYxACRxWR,
  output nVDPxWR,
  output nVDPxRD,
  output nCSxPSGxWR,
  output nCSxPSGxA0,
  output nCSxACRxWR,
  output nCSxACR,
  output nODELAYxACRxWR
);

  wire not_1_out, not_2_out, or_1_out, or_2_out, or_3_out;

  not not_1 (not_1_out, bA2);
  or or_1 (or_1_out, nCSxMEDIA, bA2);
  or or_2 (or_2_out, nCSxMEDIA, not_1_out);
  not not_2 (not_2_out, bA1);
  or or_3 (or_3_out, or_2_out, bA1);
  or or_4 (nCSxACR, or_2_out, not_2_out);
  or or_5 (nVDPxWR, nbWR, or_1_out);
  or or_6 (nVDPxRD, or_1_out, nbRD);
  nor nor_1 (nCSxPSGxWR, nbWR, or_3_out);
  nor nor_2 (nCSxPSGxA0, or_3_out, bA0);
  nor nor_3 (nODELAYxACRxWR, nCSxACR, nbWR);

  assign nCSxACRxWR = nIDELAYxACRxWR;

  // Notes on the sheet:
  //   nCSxMEDIA: pin 3
  //   bA2: pin 5
  //   bA1: pin 7
  //   nbWR: pin 2
  //   bA0: pin 6
  //   nbRD: pin 4
  //   nVDPxWR: pin 19
  //   nVDPxRD: pin 18
  //   nCSxPSGxWR: pin 17
  //   nCSxPSGxA0: pin 16
  //   nCSxACRxWR: pin 15
  //   nCSxACR: pin 14
  //   nIDELAYxACRxWR: pin 8
  //   nODELAYxACRxWR: pin 12
  //   ~CSxVDP
  //   MEDIA CS V2 GAL16V8
  //   ~CSxPSG
endmodule
