// Digital circuit GDC-MISC-GAL.dig as structural Verilog
module GDC_MISC_GAL (
  input  nDBINxGDC,
  input  nALE2,
  input  _2xWCLK,
  input  HSYNC,
  input  VSYNC,
  output nREADxVRAM,
  output nDBIN,
  output H_plus_VSYNC
);

  wire or_2_out;

  or or_1 (nDBIN, nDBINxGDC, nDBINxGDC);
  or or_2 (or_2_out, nALE2, _2xWCLK);
  and and_1 (H_plus_VSYNC, HSYNC, VSYNC);
  and and_2 (nREADxVRAM, nDBIN, or_2_out);

  // Notes on the sheet:
  //   nDBINxGDC: pin 2
  //   nALE2: pin 3
  //   _2xWCLK: pin 4
  //   nREADxVRAM: pin 18
  //   nDBIN: pin 19
  //   HSYNC: pin 5
  //   VSYNC: pin 6
  //   H_plus_VSYNC: pin 17
  //   GDC MISC GAL16V8
endmodule
