// Digital circuit DUALESP32 GAL.dig as structural Verilog
module DUALESP32_GAL (
  input  nCSxESP,
  input  nbRD,
  input  nbWR,
  input  bA0,
  input  bA1,
  output nPRExESP0xRD,
  output nPRExESP1xRD,
  output nPRExESP0xWR,
  output nPRExESP1xWR,
  output nESPxSTAT
);

  wire not_1_out, not_2_out, or_1_out, or_2_out, or_3_out, or_4_out, or_5_out;

  or or_1 (or_1_out, nCSxESP, nbRD);
  or or_2 (or_2_out, nCSxESP, nbWR);
  not not_1 (not_1_out, bA0);
  not not_2 (not_2_out, bA1);
  or or_3 (or_3_out, bA1, or_1_out);
  or or_4 (or_4_out, bA1, or_2_out);
  or or_5 (or_5_out, not_2_out, nCSxESP);
  or or_6 (nPRExESP0xRD, bA0, or_3_out);
  or or_7 (nPRExESP1xRD, or_3_out, not_1_out);
  or or_8 (nPRExESP0xWR, bA0, or_4_out);
  or or_9 (nPRExESP1xWR, or_4_out, not_1_out);
  or or_10 (nESPxSTAT, or_5_out, nbRD);

  // Notes on the sheet:
  //   nCSxESP: pin 2
  //   nbRD: pin 3
  //   nbWR: pin 4
  //   bA0: pin 5
  //   bA1: pin 6
  //   nPRExESP0xRD: pin 19
  //   nPRExESP1xRD: pin 18
  //   nPRExESP0xWR: pin 17
  //   nPRExESP1xWR: pin 16
  //   nESPxSTAT: pin 15
  //   DUALESP32 GAL16V8
  //   ESP RD
  //   ESP WR
endmodule
