// Digital circuit TMS9995-IO-FIX.dig as structural Verilog
module TMS9995_IO_FIX (
  input  CPU_A5,
  input  CPU_A3,
  input  CPU_A4,
  input  CPU_A2,
  input  nCFSEL,
  input  nMAPSEL,
  output nMAPSEL16,
  output nCFSEL4
);

  or or_1 (nMAPSEL16, nMAPSEL, CPU_A4, CPU_A5);
  or or_2 (nCFSEL4, CPU_A5, CPU_A4, CPU_A3, CPU_A2, nCFSEL);

  // Notes on the sheet:
  //   CPU_A5: pin 3
  //   CPU_A3: pin 5
  //   CPU_A4: pin 4
  //   CPU_A2: pin 6
  //   nCFSEL: pin 7
  //   nMAPSEL: pin 2
  //   nMAPSEL16: pin 19
  //   nCFSEL4: pin 18
endmodule
