// Digital circuit SAB80535-CS-1.dig as structural Verilog
module SAB80535_CS_1 (
  input  A2,
  input  A3,
  input  A4,
  input  nY0,
  input  nIOxSEL,
  input  ZA19,
  input  nWR,
  output nCSxRAM,
  output nCSxPPI0,
  output nCSxPPI1,
  output nCSxMMUxWR,
  output nCSxLCD,
  output nCSxROM
);

  wire _74138_1_p12, not_1_out;

  // _74138 _74138_1: pin names not known; wires that end beside it: A2, A3, A4, 1'b1, 1'b0, nY0, 1'b1, 1'b0, nCSxPPI0, nCSxPPI1, nCSxLCD, _74138_1_p12
  not not_1 (not_1_out, ZA19);
  nand nand_1 (nCSxRAM, nIOxSEL, ZA19);
  nand nand_2 (nCSxROM, not_1_out, nIOxSEL);
  or or_1 (nCSxMMUxWR, _74138_1_p12, nWR);

  // Notes on the sheet:
  //   nCSxRAM: pin 15
  //   A2: pin 2
  //   A3: pin 3
  //   A4: pin 4
  //   nCSxPPI0: pin 19
  //   nCSxPPI1: pin 18
  //   nCSxMMUxWR: pin 16
  //   nCSxLCD: pin 17
  //   nY0: pin 5
  //   nIOxSEL: pin 6
  //   ZA19: pin 7
  //   nWR: pin 8
  //   nCSxROM: pin 14
  //   SAB80535 CS 1 GAL16V8
endmodule
