// Digital circuit SAB80535-CS-V2.dig as structural Verilog
module SAB80535_CS_V2 (
  input  A2,
  input  A3,
  input  A4,
  input  nY0,
  input  nIOxSEL,
  input  A19,
  input  nWR,
  output nCSxRAM,
  output nCSxPPI0,
  output nCSxPPI1,
  output nCSxMMU,
  output nCSxUSBxSD,
  output nCSxI2C,
  output nCSxFF,
  output nCSxLCD,
  output nCSxLATCH,
  output A
);

  wire _74138_1_p12, _74138_1_p15;

  // _74138 _74138_1: pin names not known; wires that end beside it: A2, A3, A4, 1'b1, 1'b0, nY0, 1'b1, 1'b0, nCSxPPI0, nCSxPPI1, nCSxLCD, _74138_1_p12, nCSxUSBxSD, nCSxI2C, _74138_1_p15, nCSxLATCH
  nand nand_1 (nCSxRAM, nIOxSEL, A19);
  or or_1 (nCSxMMU, _74138_1_p12, nWR);
  or or_2 (nCSxFF, _74138_1_p15, nWR);
  or or_3 (A, nCSxI2C, nWR);

  // Notes on the sheet:
  //   nCSxRAM: pin 14
  //   A2: pin 2
  //   A3: pin 3
  //   A4: pin 4
  //   nCSxPPI0: pin 23
  //   nCSxPPI1: pin 22
  //   nCSxMMU: pin 20
  //   nCSxUSBxSD: pin 19
  //   nCSxI2C: pin 18
  //   nCSxFF: pin 17
  //   nCSxLCD: pin 21
  //   nCSxLATCH: pin 16
  //   nY0: pin 5
  //   nIOxSEL: pin 6
  //   A19: pin 7
  //   nWR: pin 8
  //   A: pin 15
  //   SAB80535 CS V2 GAL22V10
endmodule
