// Digital circuit SAB80535-CS.dig as structural Verilog
module SAB80535_CS (
  input  A11,
  input  A12,
  input  A13,
  input  A14,
  input  A15,
  input  A8,
  input  A9,
  input  A10,
  input  nCSxLCDxWR,
  output nCSxROM,
  output nCSxPPI0,
  output nCSxPPI1,
  output nCSxP0,
  output nCSxP1,
  output nCSxP2,
  output nCSxP3,
  output nCSxLCD,
  output nCSxLATCH,
  output E
);

  wire nand_1_out, not_1_out;

  nand nand_1 (nand_1_out, A11, A12, A13, A14);
  not not_1 (not_1_out, nCSxLCDxWR);
  // _74138 _74138_1: pin names not known; wires that end beside it: A8, A9, A10, A15, 1'b0, nand_1_out, 1'b1, 1'b0, nCSxPPI0, nCSxPPI1, nCSxP0, nCSxP1, nCSxP2, nCSxP3, nCSxLCD, nCSxLATCH
  nand nand_2 (nCSxROM, nand_1_out, A15);
  not not_2 (E, not_1_out);

  // Notes on the sheet:
  //   A11: pin 2
  //   A12: pin 3
  //   A13: pin 4
  //   A14: pin 5
  //   A15: pin 6
  //   nCSxROM: pin 23
  //   A8: pin 7
  //   A9: pin 8
  //   A10: pin 9
  //   nCSxPPI0: pin 22
  //   nCSxPPI1: pin 21
  //   nCSxP0: pin 20
  //   nCSxP1: pin 19
  //   nCSxP2: pin 18
  //   nCSxP3: pin 17
  //   nCSxLCD: pin 16
  //   nCSxLATCH: pin 15
  //   nCSxLCDxWR: pin 10
  //   E: pin 14
  //   ~ADDRxSEL
  //   SAB80535 CS GAL22V10
endmodule
