// Digital circuit SAB80535-RX-TX.dig as structural Verilog
module SAB80535_RX_TX (
  input  nRD,
  input  nPSEN,
  input  nWR,
  input  TxD,
  input  TO,
  input  RxDx1,
  input  RxDx0,
  input  nCSxLCD,
  output nOE,
  output CSxLCDxWR,
  output TXxLED,
  output RXxLED,
  output TxDx0,
  output TxDx1,
  output RxD
);

  wire and_2_out, nor_1_out, nor_2_out, not_1_out, not_2_out, not_4_out;

  and and_1 (nOE, nRD, nPSEN);
  and and_2 (and_2_out, nOE, nWR);
  not not_1 (not_1_out, TxD);
  not not_2 (not_2_out, TO);
  nand nand_1 (TxDx0, not_1_out, not_2_out);
  nand nand_2 (TxDx1, not_1_out, TO);
  nor nor_1 (nor_1_out, TO, RxDx1);
  nor nor_2 (nor_2_out, not_2_out, RxDx0);
  nor nor_3 (CSxLCDxWR, and_2_out, nCSxLCD);
  not not_3 (TXxLED, not_1_out);
  nor nor_4 (RxD, nor_1_out, nor_2_out);
  not not_4 (not_4_out, RxD);
  not not_5 (RXxLED, not_4_out);

  // Notes on the sheet:
  //   nRD: pin 2
  //   nPSEN: pin 3
  //   nOE: pin 19
  //   nWR: pin 4
  //   CSxLCDxWR: pin 18
  //   TxD: pin 6
  //   TXxLED: pin 17
  //   RXxLED: pin 12
  //   TO: pin 7
  //   TxDx0: pin 15
  //   TxDx1: pin 14
  //   RxDx1: pin 8
  //   RxDx0: pin 9
  //   RxD: pin 13
  //   nCSxLCD: pin 5
  //   SAB80535 RX TX GAL16V8
  //   ~TxD
  //   ~TO
  //   ~OExWR
  //   ~Rx1
  //   ~Rx0
endmodule
