// Digital circuit SAB80535-CPLD.dig as structural Verilog
module SAB80535_CPLD (
  input  nRD,
  input  nPSEN,
  input  nWR,
  input  TxD,
  input  TO,
  input  nRxDx1,
  input  nRxDx0,
  input  A11,
  input  A12,
  input  A13,
  input  A14,
  input  A15,
  input  A8,
  input  A9,
  input  A10,
  output nOE,
  output nCSxLCDxWR,
  output nTXxLED,
  output RXxLED,
  output nTO,
  output nTxDx0,
  output nTxDx1,
  output RxD,
  output nCSxROM,
  output nCSxPPI0,
  output nCSxPPI1,
  output nCSxP0,
  output nCSxP1,
  output nCSxP2,
  output nCSxP3,
  output nCSxLCD
);

  wire and_2_out, nand_3_out, nor_1_out, nor_2_out, not_1_out, not_4_out;

  and and_1 (nOE, nRD, nPSEN);
  and and_2 (and_2_out, nOE, nWR);
  not not_1 (not_1_out, TxD);
  not not_2 (nTO, TO);
  nand nand_1 (nTxDx0, not_1_out, nTO);
  nand nand_2 (nTxDx1, not_1_out, TO);
  nor nor_1 (nor_1_out, TO, nRxDx1);
  nor nor_2 (nor_2_out, nTO, nRxDx0);
  nand nand_3 (nand_3_out, A11, A12, A13, A14);
  // _74138 _74138_1: pin names not known; wires that end beside it: A8, A9, A10, A15, 1'b0, nand_3_out, 1'b1, 1'b0, nCSxPPI0, nCSxPPI1, nCSxP0, nCSxP1, nCSxP2, nCSxP3, nCSxLCD
  nor nor_3 (nCSxLCDxWR, and_2_out, nCSxLCD);
  not not_3 (nTXxLED, not_1_out);
  nor nor_4 (RxD, nor_1_out, nor_2_out);
  nand nand_4 (nCSxROM, nand_3_out, A15);
  not not_4 (not_4_out, RxD);
  not not_5 (RXxLED, not_4_out);

  // Notes on the sheet:
  //   ~ADDRxSEL
  //   ~TxD
  //   ~TO
  //   ~OExWR
  //   ~Rx1
  //   ~Rx0
endmodule
