// Digital circuit Z80-processor-CPU.dig as structural Verilog
module Z80_processor_CPU (
  input  IOxSEL,
  input  nCPUxRD,
  input  nDMAxIEI1,
  input  nCPUxM1,
  input  nCPUxIORQ,
  input  nDMAxIEO2,
  input  nFPxLATCH,
  input  nCPUxWR,
  input  CPU_A2,
  input  nCSxMAP,
  input  CPU_A14,
  input  mA14,
  input  CPU_A15,
  input  mA15,
  input  CPU_A1,
  input  nINTxI2C,
  input  nA,
  input  WSxMEMRD,
  input  WSxIORD,
  input  WSxMEMWR,
  input  WSxIOWR,
  input  nCPUxMREQ,
  input  nCPUxRFSH,
  input  CPU_D0,
  input  nEIRQ7,
  input  nEIRQ6,
  input  nEIRQ0,
  input  nEIRQ1,
  input  nEIRQ2,
  input  nEIRQ3,
  input  nEIRQ5,
  input  nEIRQ4,
  input  CLK,
  input  nCPUxRESET,
  output DATAxDIR,
  output nIM2xEN,
  output nFPxLATCHxRD,
  output FPxLATCHxWR,
  output nIM2xIEO,
  output SEL_A14,
  output SEL_A15,
  output nCSxI2C,
  output INT_I2C,
  output nCSxI2CxWR,
  output nAxPRIME,
  output READY,
  output nPAGExEN,
  output nPAGExWR,
  output IM2xS2,
  output IM2xS1,
  output IM2xS0,
  output nIM2xINT,
  output _1WS,
  output _2WS,
  output _3WS,
  output _4WS,
  output _5WS,
  output _6WS,
  output _7WS,
  output _8WS,
  output RESET
);

  wire _74139_1_p10, _74139_1_p11, _74153_1_p15, and_2_out, d_ff_as_1_nq, nand_1_out, nand_2_out, not_1_out,
       not_2_out, not_5_out, or_1_out, or_4_out, or_5_out, or_6_out, or_9_out;

  not not_1 (not_1_out, nDMAxIEI1);
  not not_2 (not_2_out, nDMAxIEO2);
  nand nand_1 (nand_1_out, nCPUxMREQ, nCPUxIORQ);
  nand nand_2 (nand_2_out, nand_1_out, nCPUxRFSH);
  or or_1 (or_1_out, nCPUxM1, nCPUxIORQ);
  or or_2 (nIM2xIEO, nIM2xINT, not_2_out);
  or or_3 (nFPxLATCHxRD, nCPUxRD, nFPxLATCH);
  or or_4 (or_4_out, nFPxLATCH, nCPUxWR);
  // _74148 _74148_1: pin names not known; wires that end beside it: 1'b0, nEIRQ7, nEIRQ6, nEIRQ5, nEIRQ4, nEIRQ3, nEIRQ2, nEIRQ1, nEIRQ0, 1'b1, 1'b0, IM2xS2, IM2xS1, IM2xS0, nIM2xINT
  // _74153 _74153_1: pin names not known; wires that end beside it: 1'b0, WSxMEMRD, WSxIORD, WSxMEMWR, WSxIOWR, 1'b1, 1'b1, 1'b1, 1'b1, 1'b1, nCPUxMREQ, nCPUxRD, 1'b1, 1'b0, _74153_1_p15
  or or_5 (or_5_out, nCPUxRD, IOxSEL);
  or or_6 (or_6_out, or_1_out, not_1_out);
  or or_7 (nIM2xEN, or_1_out, nIM2xIEO);
  not not_3 (FPxLATCHxWR, or_4_out);
  or or_8 (READY, nand_2_out, _74153_1_p15);
  and and_1 (DATAxDIR, or_5_out, or_6_out);
  // _74164 _74164_1: pin names not known; wires that end beside it: CLK, 1'b1, 1'b1, nand_1_out, 1'b1, 1'b0, _1WS, _2WS, _3WS, _4WS, _5WS, _6WS, _7WS, _8WS
  D_FF_AS d_ff_as_1 (.Set(~1'b1), .D(CPU_D0), .C(or_9_out), .Clr(~nCPUxRESET), .nQ(d_ff_as_1_nq));  // open: Q
  not not_4 (RESET, nCPUxRESET);
  not not_5 (not_5_out, CPU_A1);
  not not_6 (INT_I2C, nINTxI2C);
  and and_2 (and_2_out, ~1'b1, ~nCPUxRESET);  // And
  // _74139 _74139_1: pin names not known; wires that end beside it: nCPUxWR, CPU_A2, nCSxMAP, 1'b0, CPU_A2, nCSxMAP, 1'b1, 1'b0, nPAGExWR, _74139_1_p10, _74139_1_p11
  // _74157 _74157_1: pin names not known; wires that end beside it: CPU_A14, CPU_A15, 1'b1, 1'b1, mA14, mA15, 1'b1, 1'b1, nCPUxIORQ, 1'b0, 1'b1, 1'b0, SEL_A14, SEL_A15
  or or_9 (or_9_out, _74139_1_p10, CPU_A1);
  or or_10 (nCSxI2C, _74139_1_p11, not_5_out);
  or or_11 (nAxPRIME, nCSxI2C, nCPUxWR);
  or or_12 (nPAGExEN, d_ff_as_1_nq, and_2_out);

  assign nCSxI2CxWR = nA;

  // Notes on the sheet:
  //   CPU DATA DIR GAL22V10
  //   CPU WS GAL16V8
  //   ~INTA
  //   RDY
  //   ~MR
  //   HIGH A->B
  //   LOW B->A
  //   7474 Replacement
  //   NOTE: CONNECT ~A~ to ~AxPRIME~
  //   WITH PHYSICAL WIRE
  //   CPU MAPPER V2 GAL22V10
  //   ~PGENxWR
endmodule
