// Digital circuit Z80-processor-DMA.dig as structural Verilog
module Z80_processor_DMA (
  input  CPUxA0,
  input  CPUxA1,
  input  nCPUxWAIT,
  input  nBUSRQ,
  input  nCPUxBUSACK,
  input  nDMAxINTxPULSE1,
  input  nDMAxINTxPULSE2,
  input  CPUxA3,
  input  nDREQ0,
  input  nDREQ1,
  input  nCPUxWR,
  input  nCPUxRESET,
  input  nDMAxBAO2,
  input  CPU_D0,
  input  CPU_D1,
  input  CPU_D2,
  input  CPU_D3,
  input  nCPUxIORQ,
  input  nCPUxM1,
  input  CPUxA2,
  input  Q2,
  input  Q3,
  input  CPUxA4,
  input  CPUxA5,
  input  CPUxA6,
  input  CPUxA7,
  input  Q4,
  input  Q5,
  input  Q6,
  input  Q7,
  input  R4,
  input  R5,
  input  R6,
  input  R7,
  output nFPxLATCH,
  output nDMAxCS1,
  output nDMAxCS2,
  output nBUSxEN,
  output DATAxXFER,
  output IOxSEL,
  output nCSxMAP,
  output nCSxUART,
  output DMAxRDY1,
  output DMAxRDY2,
  output nDMAxRESET1,
  output nDMAxRESET2,
  output BUSACK
);

  wire _74139_1_p11, _74139_1_p12, _74139_1_p14, _74157_1_p13, _74157_1_p14, _74175_1_p9, _74175_1_p10,
       _74175_1_p11, _74175_1_p12, _74688_1_p18, _74688_2_p20, and_1_out, and_2_out, not_1_out, not_2_out,
       not_3_out, not_4_out, or_1_out, or_9_out;

  not not_1 (not_1_out, CPUxA3);
  // _74688 _74688_1: pin names not known; wires that end beside it: nCPUxIORQ, nCPUxM1, 1'b1, 1'b1, 1'b1, CPUxA2, Q2, CPUxA3, Q3, CPUxA4, Q4, CPUxA5, Q5, CPUxA6, Q6, CPUxA7, Q7, _74688_1_p18
  // _74139 _74139_1: pin names not known; wires that end beside it: 1'b1, 1'b0, 1'b1, 1'b1, 1'b1, _74688_1_p18, CPUxA0, CPUxA1, 1'b1, 1'b0, _74139_1_p11, _74139_1_p12, nFPxLATCH, _74139_1_p14
  not not_2 (not_2_out, nCPUxBUSACK);
  // _74157 _74157_1: pin names not known; wires that end beside it: nCPUxWAIT, nCPUxWAIT, 1'b0, 1'b0, _74139_1_p11, _74139_1_p12, 1'b0, 1'b0, nBUSRQ, 1'b0, 1'b1, 1'b0, _74157_1_p13, _74157_1_p14
  and and_1 (and_1_out, nDMAxCS1, nDMAxCS2);
  or or_1 (or_1_out, nCPUxBUSACK, nBUSRQ);
  and and_2 (and_2_out, nDMAxINTxPULSE1, nDMAxINTxPULSE2);
  nand nand_1 (IOxSEL, _74688_1_p18, _74688_2_p20);
  or or_2 (nCSxMAP, _74688_2_p20, CPUxA3);
  or or_3 (nCSxUART, _74688_2_p20, not_1_out);
  or or_4 (nDMAxCS1, not_2_out, _74157_1_p13);
  or or_5 (nDMAxCS2, not_2_out, _74157_1_p14);
  nand nand_2 (nBUSxEN, nCPUxBUSACK, and_1_out);
  or or_6 (DATAxXFER, or_1_out, and_2_out);
  not not_3 (not_3_out, nDREQ0);
  not not_4 (not_4_out, nDREQ1);
  // _74688 _74688_2: pin names not known; wires that end beside it: nCPUxIORQ, nCPUxM1, 1'b1, 1'b1, 1'b1, 1'b1, 1'b1, 1'b1, 1'b1, CPUxA4, R4, CPUxA5, R5, CPUxA6, R6, CPUxA7, R7, 1'b1, 1'b0, _74688_2_p20
  or or_7 (DMAxRDY1, not_3_out, _74175_1_p9);
  or or_8 (DMAxRDY2, not_4_out, _74175_1_p10);
  or or_9 (or_9_out, nCPUxWR, _74139_1_p14);
  // _74175 _74175_1: pin names not known; wires that end beside it: CPU_D0, CPU_D1, CPU_D2, CPU_D3, or_9_out, nCPUxRESET, 1'b1, 1'b0, _74175_1_p9, _74175_1_p10, _74175_1_p11, _74175_1_p12
  not not_5 (BUSACK, nDMAxBAO2);
  and and_3 (nDMAxRESET1, _74175_1_p11, nCPUxRESET);
  and and_4 (nDMAxRESET2, nCPUxRESET, _74175_1_p12);

  // Notes on the sheet:
  //   DMA CS V2
  //   ~DMAxADDR
  //   DMA RDY
  //   ~CSxIO
  //   RDY1
  //   ~USRxRESET1
  //   ~USRxRESET2
  //   ~DMAxRDYxWR
  //   RDY2
endmodule
